// Digital circuit ADDER.dig as structural Verilog
module ADDER (
  input  Inp_0,
  input  Inp_1,
  input  Inp_0_2,
  input  Inp_1_2,
  input  Inp_Carry,
  input  Inp_0_3,
  input  Inp_1_3,
  input  Inp_Carry_2,
  input  Inp_2,
  input  Inp_3,
  input  Inp_Carry_3,
  input  Inp_2_2,
  input  Inp_3_2,
  input  Inp_4,
  input  Inp_5,
  input  Inp_6,
  input  Inp_7,
  input  Inp_0_4,
  input  Inp_1_4,
  input  Inp_Carry_4,
  input  Inp_2_3,
  input  Inp_3_3,
  input  Inp_8,
  input  Inp_9,
  input  Inp_10,
  input  Inp_11,
  output Sum,
  output Carry,
  output Carry_2,
  output Sum_4,
  output Sum_5,
  output Carry_3,
  output Sum_0,
  output Sum_1,
  output Sum_2,
  output Sum_3,
  output Carry_4,
  output Sum_0_2,
  output Sum_1_2,
  output Sum_2_2,
  output Sum_3_2,
  output Carry_Bit
);

  wire add_1_c_o, add_2_c_o, add_3_c_o, add_6_c_o, add_6_s, and_2_out, and_3_out, and_4_out, and_5_out,
       and_6_out, and_7_out, and_8_out, and_9_out, and_10_out, and_11_out, or_1_out, or_2_out, or_5_out,
       xor_2_out, xor_3_out, xor_4_out, xor_5_out, xor_6_out;

  Add add_1 (.a(Inp_2), .b(Inp_3), .c_i(Inp_Carry_3), .s(Sum_0), .c_o(add_1_c_o));
  Add add_2 (.a(Inp_2_2), .b(Inp_3_2), .c_i(add_1_c_o), .s(Sum_1), .c_o(add_2_c_o));
  Add add_3 (.a(Inp_4), .b(Inp_5), .c_i(add_2_c_o), .s(Sum_2), .c_o(add_3_c_o));
  Add add_4 (.a(Inp_6), .b(Inp_7), .c_i(add_3_c_o), .s(Sum_3), .c_o(Carry_4));
  xor xor_1 (Sum, Inp_0, Inp_1);
  and and_1 (Carry, Inp_1, Inp_0);
  xor xor_2 (xor_2_out, Inp_0_4, Inp_1_4);
  and and_2 (and_2_out, Inp_1_4, Inp_0_4);
  xor xor_3 (xor_3_out, Inp_2_3, Inp_3_3);
  and and_3 (and_3_out, Inp_3_3, Inp_2_3);
  xor xor_4 (xor_4_out, Inp_8, Inp_9);
  and and_4 (and_4_out, Inp_9, Inp_8);
  xor xor_5 (xor_5_out, Inp_10, Inp_11);
  and and_5 (and_5_out, Inp_11, Inp_10);
  xor xor_6 (xor_6_out, Inp_0_2, Inp_1_2);
  and and_6 (and_6_out, Inp_1_2, Inp_0_2);
  Add add_5 (.a(Inp_0_3), .b(Inp_1_3), .c_i(Inp_Carry_2), .s(Sum_5), .c_o(Carry_3));
  and and_7 (and_7_out, xor_2_out, Inp_Carry_4);
  and and_8 (and_8_out, xor_3_out, or_1_out);
  and and_9 (and_9_out, xor_4_out, or_5_out);
  and and_10 (and_10_out, xor_5_out, or_2_out);
  and and_11 (and_11_out, xor_6_out, Inp_Carry);
  Add add_6 (.a(Inp_0), .b(Inp_1), .c_i(1'b0), .s(add_6_s), .c_o(add_6_c_o));
  or or_1 (or_1_out, and_2_out, and_7_out);
  or or_2 (or_2_out, and_4_out, and_9_out);
  or or_3 (Carry_Bit, and_5_out, and_10_out);
  or or_4 (Carry_2, and_6_out, and_11_out);
  xor xor_7 (Sum_0_2, xor_2_out, Inp_Carry_4);
  or or_5 (or_5_out, and_3_out, and_8_out);
  xor xor_8 (Sum_1_2, xor_3_out, or_1_out);
  xor xor_9 (Sum_2_2, xor_4_out, or_5_out);
  xor xor_10 (Sum_3_2, xor_5_out, or_2_out);
  xor xor_11 (Sum_4, xor_6_out, Inp_Carry);

  // Notes on the sheet:
  //   Multi Bit adder w/ not allowed adder
  //   functions just to show expected
  //   output
  //   Toby's Multi bit adder
  //   Tobys Full Adder
endmodule
