// Digital circuit FA.dig as structural Verilog
module FA (
  input  Inp_0,
  input  Inp_1,
  input  Inp_0_2,
  input  Inp_1_2,
  input  Inp_Carry,
  input  Inp_0_3,
  input  Inp_1_3,
  input  Inp_Carry_2,
  output Sum,
  output Carry,
  output Carry_2,
  output Sum_2,
  output Sum_3,
  output Carry_3
);

  wire add_2_c_o, add_2_s, and_2_out, and_3_out, xor_2_out;

  xor xor_1 (Sum, Inp_0, Inp_1);
  and and_1 (Carry, Inp_1, Inp_0);
  xor xor_2 (xor_2_out, Inp_0_2, Inp_1_2);
  and and_2 (and_2_out, Inp_1_2, Inp_0_2);
  Add add_1 (.a(Inp_0_3), .b(Inp_1_3), .c_i(Inp_Carry_2), .s(Sum_3), .c_o(Carry_3));
  and and_3 (and_3_out, xor_2_out, Inp_Carry);
  Add add_2 (.a(Inp_0), .b(Inp_1), .c_i(1'b0), .s(add_2_s), .c_o(add_2_c_o));
  or or_1 (Carry_2, and_2_out, and_3_out);
  xor xor_3 (Sum_2, xor_2_out, Inp_Carry);

  // Notes on the sheet:
  //   Tobys Full Adder
endmodule
