// Digital circuit HA.dig as structural Verilog
module HA (
  input  Inp_0,
  input  Inp_1,
  output Sum,
  output Carry
);

  xor xor_1 (Sum, Inp_0, Inp_1);
  and and_1 (Carry, Inp_1, Inp_0);

  // Notes on the sheet:
  //   Toby's Half adder
endmodule
