// Digital circuit SIMPLY (1).dig as structural Verilog
module SIMPLY__1 (
  input  clk,
  output [7:0] PC,
  output [7:0] Function,
  output BRA,
  output BZ,
  output LD,
  output LDI,
  output ST,
  output ADD,
  output HLT,
  output [7:0] Value_now_in_register_R,
  output [7:0] Next_PC,
  output [7:0] imm,
  output [2:0] instr__class,
  output [1:0] out_15,
  output [1:0] out_16,
  output [7:0] out_17,
  output [7:0] out_18,
  output BRA_2,
  output BZ_2,
  output LD_2,
  output LDI_2,
  output ST_2,
  output ADD_2,
  output HLT_2,
  output out_26,
  output out_27,
  output out_28
);

  wire and_1_out, and_2_out, and_3_out, and_4_out, comparator_1_eq, decoder_1_out_6, LDI_Toggle,
       multiplexer_1_out, nand_1_out, not_1_out, not_2_out, not_3_out, not_4_out, or_1_out, or_2_out,
       or_3_out, ST_Toggle;
  wire [1:0] multiplexer_3_out, multiplexer_4_out, nfet_6_d;
  wire [3:0] nfet_1_s;
  wire [7:0] add_1_s, add_4_s, BRA_RES, BZ_RES, Mem_S__content, multiplexer_2_out, multiplexer_5_out,
       multiplexer_8_out, nfet_2_s, nfet_4_d, nfet_5_s, pfet_1_d, pfet_1_s, pfet_2_d, pfet_3_d, S_Reg_Add;

  Multiplexer multiplexer_1 (.sel(imm[4]), .in_0(1'b1), .in_1(1'b0), .out(multiplexer_1_out));
  NFET #(.Bits(4)) nfet_1 (.G(imm[4]), .D(imm[3:0]), .S(nfet_1_s));
  Multiplexer #(.Bits(8)) multiplexer_2 (.sel(imm[4]), .in_0(imm), .in_1({4'b1111, nfet_1_s}), .out(multiplexer_2_out));
  Multiplexer #(.Bits(2)) multiplexer_3 (.sel(BZ), .in_0(2'b00), .in_1(2'b01), .out(multiplexer_3_out));
  Multiplexer #(.Bits(2)) multiplexer_4 (.sel(BRA), .in_0(multiplexer_3_out), .in_1(2'b10), .out(multiplexer_4_out));
  nand nand_1 (nand_1_out, or_1_out, or_1_out);
  NFET #(.Bits(8)) nfet_2 (.G(nand_1_out), .D(8'h1), .S(nfet_2_s));
  Add #(.Bits(8)) add_1 (.a({8{1'b0}}), .b(multiplexer_2_out), .c_i(multiplexer_1_out), .s(add_1_s));  // open: c_o
  Stop stop_1 (.stop(HLT));
  NFET #(.Bits(8)) nfet_3 (.G(BRA), .D(add_1_s), .S(BRA_RES));
  or or_1 (or_1_out, BZ, BRA);
  Multiplexer #(.Selector_Bits(2), .Bits(8)) multiplexer_5 (
    .sel(multiplexer_4_out), .in_0({8{1'b0}}), .in_1(BZ_RES), .in_2(BRA_RES), .in_3({8{1'b0}}),
    .out(multiplexer_5_out));
  NFET #(.Bits(8)) nfet_4 (.G(or_1_out), .D(nfet_4_d), .S(nfet_2_s));
  PFET #(.Bits(8)) pfet_1 (.G(BRA), .S(pfet_1_s), .D(pfet_1_d));
  Multiplexer #(.Bits(8)) multiplexer_6 (.sel(or_1_out), .in_0(pfet_1_d), .in_1(multiplexer_5_out), .out(nfet_4_d));
  Add #(.Bits(8)) u_add_2 (.a(PC), .b(nfet_2_s), .c_i(1'b0), .s(Next_PC));  // open: c_o
  D_FF #(.Bits(8)) u_PC (.D(Next_PC), .C(clk), .Q(PC));  // open: nQ
  Comparator #(.Bits(8)) comparator_1 (.a(out_17), .b({8{1'b0}}), .eq(comparator_1_eq));  // open: gt, lt
  Add #(.Bits(8)) add_3 (.a(PC), .b(8'h1), .c_i(1'b0), .s(pfet_1_s));  // open: c_o
  NFET #(.Bits(8)) nfet_5 (.G(BZ), .D(imm), .S(nfet_5_s));
  Multiplexer #(.Bits(8)) multiplexer_7 (.sel(comparator_1_eq), .in_0(8'h1), .in_1(nfet_5_s), .out(BZ_RES));
  ROM #(.AddrBits(8), .isProgramMemory("true"), .Bits(8)) rom_1 (.A(PC), .sel(1'b1), .D(Function));
  NFET #(.Bits(2)) nfet_6 (.G(BZ), .D(nfet_6_d), .S(2'b01));
  Multiplexer #(.Bits(8)) multiplexer_8 (
    .sel(LD), .in_0({{6{1'b0}}, Function[3:2]}), .in_1(out_18), .out(multiplexer_8_out));
  PFET #(.Bits(8)) pfet_2 (.G(LDI), .S(Mem_S__content), .D(pfet_2_d));
  NFET #(.Bits(8)) nfet_7 (.G(LDI), .D(pfet_2_d), .S(imm));
  or or_2 (or_2_out, BZ, LDI, out_26, ADD);
  NFET #(.Bits(2)) nfet_8 (.G(LDI), .D(nfet_6_d), .S(2'b00));
  RAMDualPort #(.AddrBits(8), .Bits(8)) ramdualport_1 (
    .A(multiplexer_8_out), .Din(out_17), .str(ST), .C(ST_Toggle), .ld(1'b1), .D(Mem_S__content));
  PFET #(.Bits(8)) pfet_3 (.G(out_28), .S(pfet_2_d), .D(pfet_3_d));
  NFET #(.Bits(8)) nfet_9 (.G(out_28), .D(Value_now_in_register_R), .S(pfet_3_d));
  PFET #(.Bits(2)) pfet_4 (.G(or_2_out), .S(Function[1:0]), .D(nfet_6_d));
  NFET #(.Bits(2)) nfet_10 (.G(out_26), .D(nfet_6_d), .S(Function[1:0]));
  BitExtender #(.inputBits(5), .outputBits(8)) bitextender_1 (.in(Function[4:0]), .out(imm));
  Decoder #(.Selector_Bits(3)) decoder_1 (
    .sel(Function[7:5]), .out_0(BRA), .out_1(BZ), .out_2(LD), .out_3(LDI), .out_4(ST), .out_5(ADD),
    .out_6(decoder_1_out_6), .out_7(HLT));
  or or_3 (or_3_out, out_28, LDI_Toggle, out_26);
  RegisterFile #(.Bits(8)) registerfile_1 (
    .Din(pfet_3_d), .we(or_3_out), .Rw(nfet_6_d), .C(or_3_out), .Ra(nfet_6_d), .Rb(Function[3:2]),
    .Da(out_17), .Db(out_18));
  NFET #(.Bits(2)) nfet_11 (.G(ADD), .D(nfet_6_d), .S(Function[1:0]));
  not not_1 (not_1_out, clk);
  not not_2 (not_2_out, clk);
  not not_3 (not_3_out, clk);
  not not_4 (not_4_out, clk);
  NFET #(.Bits(8)) nfet_12 (.G(LD), .D(out_18), .S(S_Reg_Add));
  and and_1 (and_1_out, not_1_out, LD);
  and and_2 (and_2_out, not_2_out, ADD);
  and and_3 (and_3_out, not_3_out, ST);
  and and_4 (and_4_out, not_4_out, LDI);
  Add #(.Bits(8)) add_4 (.a(out_17), .b(out_18), .c_i(1'b0), .s(add_4_s));  // open: c_o
  RS_FF_AS rs_ff_as_1 (.S(and_3_out), .R(clk), .Q(ST_Toggle));  // open: nQ
  RS_FF_AS rs_ff_as_2 (.S(and_4_out), .R(clk), .Q(LDI_Toggle));  // open: nQ
  RS_FF_AS rs_ff_as_3 (.S(and_1_out), .R(clk), .Q(out_26));  // open: nQ
  RS_FF_AS rs_ff_as_4 (.S(and_2_out), .R(clk), .Q(out_28));  // open: nQ
  Multiplexer #(.Bits(8)) multiplexer_9 (.sel(ADD), .in_0({8{1'b0}}), .in_1(add_4_s), .out(Value_now_in_register_R));

  assign ADD_2 = ADD;
  assign BRA_2 = BRA;
  assign BZ_2 = BZ;
  assign HLT_2 = HLT;
  assign instr__class = Function[7:5];
  assign LD_2 = LD;
  assign LDI_2 = LDI;
  assign out_15 = Function[3:2];
  assign out_16 = Function[1:0];
  assign out_27 = LDI;
  assign ST_2 = ST;

  // Other names for the same wires on the sheet: Add_t[7:0] = Function; R_reg[1:0] = Function[1:0];
  //   S_reg[1:0] = Function[3:2]; _0 = Function[4]; inst[2:0] = Function[7:5]; ADD_Toggle = out_28;
  //   LD_Toggle = out_26; R_Reg_Val[7:0] = out_17; Reg_Input[7:0] = Mem_S__content;
  //   Reg_Input_ADD[7:0] = Value_now_in_register_R; S_Reg_Val[7:0] = out_18

  // Notes on the sheet:
  //   TobyS Circuit
  //   BRA
  //   PC
  //   BZ
  //   Registers
  //   If BZ pass X1
  //   Mem Storage
  //   RAM Memory
  //   contents of rom_1 (hex, n*v repeats v):
  //   2,0,0,61,41,2c,7f,a2,60,a3,60,a4,0,a9,a3,24,1d,60,a3,a1,0,63,a1
  //   ,87,e0
  //   If LDI pass X0
  //   LD pass R reg
  //   Inst Decoder
  //   ADD pass R reg
  //   LD Write
  //   Get content of memory at address
  //   from value in register S
  //   ADD R, S
  //   ST R, [S]
  //   LD R, [S]
  //   Once we found content at mem [S]
  //   call LD write function
  //   Then call LD Write and 
  //   store that new content into
  //   register R
endmodule
